# Fritzing sketch 2_piston (saved by Fritzing 0.9.3b)
circuit board: 11.8604cm x 10.4024cm
breadboards: 3

parts:
  Parça1 = Arduino Pro Mini (5V)
  24_V = Power plug
  D3 = Rectifier Diode [part_number=1N4001 package="300 mil [THT]"]
  5_V = Power plug
  R2 = Resistor [tolerance=±5% resistance=2.2k package=THT]
  Q2 = NPN-Transistor [package="TO92 [THT]"]
  D4 = Rectifier Diode [part_number=1N4001 package="300 mil [THT]"]
  Q3 = NPN-Transistor [package="TO92 [THT]"]
  R3 = Resistor [tolerance=±5% resistance=2.2k package=THT]
  K2 = Relay [part_number=FRS1B-S package=THT]
  R4 = Resistor [tolerance=±5% resistance=2.2k package=THT]
  K3 = Relay [part_number=FRS1B-S package=THT]
  D6 = Rectifier Diode [part_number=1N4001 package="300 mil [THT]"]
  Q5 = NPN-Transistor [package="TO92 [THT]"]
  R5 = Resistor [tolerance=±5% resistance=2.2k package=THT]
  K4 = Relay [part_number=FRS1B-S package=THT]
  Start1 = Pushbutton [package=THT]
  Start2 = Pushbutton [package=THT]
  Start3 = Pushbutton [package=THT]
  Start4 = Pushbutton [package=THT]
  Start5 = Pushbutton [package=THT]
  Start6 = Pushbutton [package=THT]
  Start7 = Pushbutton [package=THT]
  D5 = Rectifier Diode [part_number=1N4001 package="300 mil [THT]"]
  Q4 = NPN-Transistor [package="TO92 [THT]"]
  D7 = Rectifier Diode [part_number=1N4001 package="300 mil [THT]"]
  Q6 = NPN-Transistor [package="TO92 [THT]"]
  R6 = Resistor [tolerance=±5% resistance=2.2k package=THT]
  K5 = Relay [part_number=FRS1B-S package=THT]
  D8 = Rectifier Diode [part_number=1N4001 package="300 mil [THT]"]
  Q7 = NPN-Transistor [package="TO92 [THT]"]
  R7 = Resistor [tolerance=±5% resistance=2.2k package=THT]
  K6 = Relay [part_number=FRS1B-S package=THT]
  hc-sr1 = hc-sr04
  K1 = Relay [part_number=FRS1B-S package=THT]

nets (from the pcb view):
  VCC: Parça1.VCC, 5_V.VCC, hc-sr1.VCC
  GND: Parça1.GND, 24_V.GND, 5_V.GND, Q2.E, Q3.E, K2.A, K3.A, Q5.E, K4.A, Start1.leg0, Start2.leg0, Start3.leg0, Start4.leg0, Start5.leg0, Start6.leg0, Start7.leg0, Q4.E, Q6.E, K5.A, Q7.E, K6.A, hc-sr1.GND, K1.A
  N1: Parça1.A2, Start7.leg1
  N2: Parça1.A1, Start6.leg1
  N3: Parça1.A0, Start5.leg1
  N4: Parça1.SCK, Start4.leg1
  N5: Parça1.MISO, Start3.leg1
  N6: Parça1.MOSI, Start2.leg1
  N7: Parça1.D10, Start1.leg1
  N8: Parça1.D9, R2.Pin_0
  N9: Parça1.D8, R3.Pin_0
  N10: Parça1.D7, R4.Pin_0
  N11: Parça1.D6, R5.Pin_0
  N12: Parça1.D5, R6.Pin_0
  N13: Parça1.D4, R7.Pin_0
  N14: Parça1.RXI, hc-sr1.Echo
  N15: Parça1.TXO, hc-sr1.Trig
  N16: D3.cathode, D4.cathode, K2.COIL2, K3.COIL2, D6.cathode, K4.COIL2, D5.cathode, D7.cathode, K5.COIL2, D8.cathode, K6.COIL2, K1.COIL2
  N17: D3.anode, Q2.C, K1.COIL1
  N18: R2.Pin_1, Q2.B
  N19: D4.anode, Q3.C, K2.COIL1
  N20: Q3.B, R3.Pin_1
  N21: K2.B, K3.B, K4.B, K5.B, K6.B, K1.B
  N22: R4.Pin_1, Q4.B
  N23: K3.COIL1, D5.anode, Q4.C
  N24: D6.anode, Q5.C, K4.COIL1
  N25: Q5.B, R5.Pin_1
  N26: D7.anode, Q6.C, K5.COIL1
  N27: Q6.B, R6.Pin_1
  N28: D8.anode, Q7.C, K6.COIL1
  N29: Q7.B, R7.Pin_1

notes:
  5 V Devre Besleme
  24 V Piston
  Piston 1 İt
  Piston 1 Çek
  Infraar
  Soğutucu Fan
  Piston 2 İt
  Piston 2 Çek
