# Fritzing sketch lamba_deneme (saved by Fritzing 0.9.3b)
circuit board: 4.90134cm x 4.68513cm
breadboards: 1

parts:
  U1 = atmega328 [package=dip]
  XTAL1 = Crystal [frequency="16 Mhz" package=THT]
  R1 = Resistor [tolerance=±5% resistance=220 package=THT]
  C1 = Capacitor [package=cap-pth-5mm]
  C2 = Capacitor [package=cap-pth-5mm]
  D1 = Rectifier Diode [package="Melf DO-213 AA [SMD]"]
  HC-SR04_Sensor_1 = HC-SR04 Ultrasonic Distance Sensor
  U2 = MLX90614 [package=to-39]
  C3 = Capacitor [package=cap-pth-5mm]
  J3 = Camdenboss CTB0158-6 [part_number=CTB0158-6 package=THT]
  Power_plug1 = Power plug

nets:
  N1: U1.RESET, R1.Pin_1, D1.anode, C3.2
  N2: U1.D0_(RX), J3.pin3
  N3: U1.D1_(TX), J3.pin2
  5V: U1.VCC, R1.Pin_0, D1.cathode, HC-SR04_Sensor_1.VCC, U2.VDD, J3.pin4, Power_plug1.VCC
  GND: U1.GND, U1.XLAT1, U1.D11_(PWM), XTAL1.pin_0, C1.1, C1.2, C2.2, HC-SR04_Sensor_1.ECHO, HC-SR04_Sensor_1.GND, U2.VSS, J3.pin6, Power_plug1.GND
  N4: U1.XLAT2, XTAL1.pin_1, C2.1
  N5: U1.D10_(PWM), HC-SR04_Sensor_1.TRIG
  N6: U1.A4, U2.SCL_VZ
  N7: U1.A5, U2.PWM_SDA
  N8: C3.1, J3.pin1
