# Fritzing sketch 7segx2TimeCountDown (saved by Fritzing 0.9.3b)
circuit board: 11.0254cm x 7.08377cm
breadboards: 1

parts:
  Parça1 = Arduino Pro Mini v13
  U1 = 74HC595 [package="DIP16 [THT]"]
  U2 = 74HC595 [part_number=birlikicin package="DIP16 [THT]"]
  7_Segment1 = 7 Segment Display [part_number=onluk]
  7_Segment2 = 7 Segment Display [part_number=birlik]
  R1 = Resistor [tolerance=±5% resistance=680 package=THT]
  R2 = Resistor [tolerance=±5% resistance=680 package=THT]
  R3 = Resistor [tolerance=±5% resistance=680 package=THT]
  R4 = Resistor [tolerance=±5% resistance=680 package=THT]
  R5 = Resistor [tolerance=±5% resistance=680 package=THT]
  R6 = Resistor [tolerance=±5% resistance=680 package=THT]
  R7 = Resistor [tolerance=±5% resistance=680 package=THT]
  R8 = Resistor [tolerance=±5% resistance=680 package=THT]
  R9 = Resistor [tolerance=±5% resistance=680 package=THT]
  R10 = Resistor [tolerance=±5% resistance=680 package=THT]
  R11 = Resistor [tolerance=±5% resistance=680 package=THT]
  R12 = Resistor [tolerance=±5% resistance=680 package=THT]
  R13 = Resistor [tolerance=±5% resistance=680 package=THT]
  R14 = Resistor [tolerance=±5% resistance=680 package=THT]

nets:
  N1: Parça1.D4, U1.ST_CP, U2.ST_CP
  N2: Parça1.D3_PWM, U1.SH_CP, U2.SH_CP
  N3: Parça1.D2, U1.DS
  N4: U1.Q1, R2.Pin_0
  N5: U1.Q2, R3.Pin_0
  N6: U1.Q3, R4.Pin_0
  N7: U1.Q4, R5.Pin_0
  N8: U1.Q5, R6.Pin_0
  N9: U1.Q6, R7.Pin_0
  GND: U1.GND, U1.OE, U2.GND, U2.OE
  N10: U1.Q7', U2.DS
  VCC: U1.MR, U1.VCC, U2.MR, U2.VCC
  N11: U1.Q0, R1.Pin_0
  N12: U2.Q1, R9.Pin_1
  N13: U2.Q2, R10.Pin_1
  N14: U2.Q3, R11.Pin_1
  N15: U2.Q4, R12.Pin_1
  N16: U2.Q5, R13.Pin_1
  N17: U2.Q6, R14.Pin_1
  N18: U2.Q0, R8.Pin_1
  N19: 7_Segment1.Segment_E, R5.Pin_1
  N20: 7_Segment1.Segment_D, R4.Pin_1
  N21: 7_Segment1.Segment_C, R3.Pin_1
  N22: 7_Segment1.Segment_B, R2.Pin_1
  N23: 7_Segment1.Segment_A, R1.Pin_1
  N24: 7_Segment1.Segment_F, R6.Pin_1
  N25: 7_Segment1.Segment_G, R7.Pin_1
  N26: 7_Segment2.Segment_E, R12.Pin_0
  N27: 7_Segment2.Segment_D, R11.Pin_0
  N28: 7_Segment2.Segment_C, R10.Pin_0
  N29: 7_Segment2.Segment_B, R9.Pin_0
  N30: 7_Segment2.Segment_A, R8.Pin_0
  N31: 7_Segment2.Segment_F, R13.Pin_0
  N32: 7_Segment2.Segment_G, R14.Pin_0

// code stored in the sketch: 7segTimeCountdown.ino
////const byte ledCharSet[10] =
////{
//// B00100001,  //0 E-F-DP-C-D-B-A-G
//// B11101011,  //1
//// B01110000,  //2
//// B11100000,  //3
//// B10101010,  //4
//// B10100100,  //5
//// B00100110,  //6
//// B11101001,  //7
//// B00100000,  //8
//// B10101000   //9
////};
//const byte ledCharSet[10] =
//{
//  B11000000,  //0 DP-G-F-E-D-C-B-A
//  B11111001,  //1
//  B10100100,  //2
//  B10110000,  //3
//  B10011001,  //4
//  B10010010,  //5
//  B10000010,  //6
//  B11111000,  //7
//  B10000000,  //8
//  B10010000   //9
//};
//
//const int latchPin = 12;
//const int clockPin = 11;
//const int dataPin = 10;
//const int K2 = 8;
//const int K1 = 9;
//void setup()
//{
//  pinMode(latchPin, OUTPUT);
//  pinMode(clockPin, OUTPUT);
//  pinMode(dataPin, OUTPUT);
//  pinMode(K1, OUTPUT);
//  pinMode(K2, OUTPUT);
//  digitalWrite(latchPin, 0);
//}
//
//void loop() {
//  for (int i = 9; i < 100 ; i++) {
//    DisplayNumber(i);
//    //delay(100);
//  }
//}
//
//void DisplayNumber(int num) {
//  int tens;
//  int ones;
//  if (num > 100 || num < 0) {
//    num = 0;
//  }
//
//  ones = num % 10;
//  if (num < 10) {
//    tens = 0;
//  }
//  else {
//    tens = num / 10;
//  }
//
//
//
//  if (num > 10) {
//    digitalWrite(K2, LOW);
//    digitalWrite(K1, HIGH);
//    digitalWrite(latchPin, 0);
//    shiftOut(dataPin, clockPin, MSBFIRST,  B00000001);
//    shiftOut(dataPin, clockPin, MSBFIRST, ledCharSet[tens]);
//    digitalWrite(latchPin, 1);
//    delay(1000);
//  }
//     digitalWrite(K1, LOW);
//    digitalWrite(K2, HIGH);
//    digitalWrite(latchPin, 0);
//    shiftOut(dataPin, clockPin, MSBFIRST,  B00000010);
//    shiftOut(dataPin, clockPin, MSBFIRST, ledCharSet[ones]);
//    digitalWrite(latchPin, 1);
//    delay(1000);
//
//
//  Serial.print(num);
//  Serial.print("\t");
//  Serial.print(tens);
//  Serial.print("\n");
//}






#define minuteLATCH 4
#define minuteCLK 3
#define minuteDATA 2

#define secondLATCH 7
#define secondCLK 6
#define secondDATA 5

//This is the hex value of each number stored in an array by index num
byte digitOne[10] = {0x3F, 0x06, 0x5B, 0x4F, 0x66, 0x6D, 0x7D, 0x07, 0x7F, 0x6F};

int minute;
int second;
boolean start;

void setup() {

  pinMode(minuteLATCH, OUTPUT);
  pinMode(minuteCLK, OUTPUT);
  pinMode(minuteDATA, OUTPUT);

  pinMode(secondLATCH, OUTPUT);
  pinMode(secondCLK, OUTPUT);
  pinMode(secondDATA, OUTPUT);

  minute = 10;
  second = 03;
  start = true;

}

void countDown ()
{
  int tens, ones, num;
  //Dakika hesaplama
  num = minute;
  ones = num % 10;
  if (num < 10) {
    tens = 0;
  }
  else {
    tens = num / 10;
  }
  displayMinuteDigits(ones, tens);

  //Saniye hesaplama
  num = second;
  ones = num % 10;
  if (num < 10) {
    tens = 0;
  }
  else {
    tens = num / 10;
  }
  displaySecondDigits(ones, tens);
}

void displaySecondDigits(int one, int ten)
{
  digitalWrite(secondLATCH, LOW);
  shiftOut(secondDATA, secondCLK, MSBFIRST, ~digitOne[one]); // digitRight
  shiftOut(secondDATA, secondCLK, MSBFIRST, ~digitOne[ten]); // digitLeft
  digitalWrite(secondLATCH, HIGH);

}

void displayMinuteDigits(int one, int ten)
{
  digitalWrite(minuteLATCH, LOW);
  shiftOut(minuteDATA, minuteCLK, MSBFIRST, ~digitOne[one]); // digitRight
  shiftOut(minuteDATA, minuteCLK, MSBFIRST, ~digitOne[ten]); // digitLeft
  digitalWrite(minuteLATCH, HIGH);

}


void loop()
{
  if (start == true)
  {
    if (second <= 0 )
    {
      minute-- ;
      second = 59;
      if (minute < 0 )
      {
        minute = 10;
        second = 00;
        start = false;
      }
    }
    countDown();
    second--;
  }
  delay(1000);
}
