# Fritzing sketch INFRAAR (saved by Fritzing 0.9.3b)
breadboards: 1

parts:
  Parça2 = Arduino Pro Mini v13  # not connected
  U1 = Graphical LCD 128x64 [package=lcd-g12864]
  CONTRAST_ADJ_1 = Trimmer Potentiometer [maximum_resistance=10kΩ package=THT]  # not connected
  VCC1 = Battery

nets:
  N1: U1.VDD, VCC1.-
  N2: U1.VSS, VCC1.+

notes:
  1 VSS - GND
  2 VDD - 5V +
  3 V0 - (contrast)
  4 RS - 36
  5 R/W - 35
  6 E - 37
  7 DB0 - 22
  8 DB1 - 23
  9 DB2 - 24
  10 DB3 - 25
  11 DB4 - 26
  12 DB5 - 27
  13 DB6 - 28
  14 DB7 - 29
  15 CS1 - 33
  16 CS2 - 34
  17 RST - 5V +
  18 VOUT - ( contrast)
  19 BLA - 5V +
  20 BLK - GND
