# Fritzing sketch IRT302N (saved by Fritzing 0.9.3b)
breadboards: 2

parts:
  U2 = Graphical LCD 128x64 [package=lcd-g12864]  # not connected
  R3 = Trimmer Potentiometer [maximum_resistance=10kΩ package=THT]  # not connected
  K2 = Relay [part_number=FRS1B-S package=THT]
  Q2 = NPN-Transistor [package="TO92 [THT]"]
  D2 = Rectifier Diode [part_number=1N4001 package="300 mil [THT]"]
  R4 = Resistor [tolerance=±5% resistance=220 package=THT]
  Power_plug2 = Power plug
  M2 = DC Motor
  Parça2 = Arduino Pro Mini (5V)

nets:
  N1: K2.A, M2.pin_1
  N2: K2.COIL1, Q2.C, D2.anode
  N3: K2.C1, K2.C2, Power_plug2.VCC
  N4: K2.COIL2, D2.cathode, Parça2.VCC
  N5: Q2.E, Parça2.GND
  N6: Q2.B, R4.Pin_0
  N7: R4.Pin_1, Parça2.D2
  N8: Power_plug2.GND, M2.pin_2
