# Fritzing sketch IRT302Nv2 (saved by Fritzing 0.9.3b)
circuit board: 16.5266cm x 10.0221cm
breadboards: 1

parts:
  CONTRAST_ADJ = Trimmer Potentiometer [maximum_resistance=10kΩ package=THT]
  GLCD_128x1 = 128 x 64 Graphic LCD
  Arduino_Mini_Pro_Rev14 = Arduino Pro Mini (5V)
  START = BUTTON-CONDUCTIVE [package=button-conductive-0.1]
  STOP = BUTTON-CONDUCTIVE [package=button-conductive-0.1]
  TEK/ÇİFT = BUTTON-CONDUCTIVE [package=button-conductive-0.1]
  PLUS = BUTTON-CONDUCTIVE [package=button-conductive-0.1]
  MINUS = BUTTON-CONDUCTIVE [package=button-conductive-0.1]
  5_V_DC = Power plug
  Relay_5V1 = keyes
  Relay_5V2 = keyes
  12_V_DC = Power plug

nets:
  N1: CONTRAST_ADJ.leg1, GLCD_128x1.18_Vout
  N2: CONTRAST_ADJ.wiper, GLCD_128x1.3_Vo
  GND: CONTRAST_ADJ.leg2, GLCD_128x1.20_K(-), Arduino_Mini_Pro_Rev14.TXO, Arduino_Mini_Pro_Rev14.RXI, Arduino_Mini_Pro_Rev14.A5, Arduino_Mini_Pro_Rev14.GND, Arduino_Mini_Pro_Rev14.MISO, Arduino_Mini_Pro_Rev14.D3, START.1, START.2, STOP.1, STOP.2, TEK/ÇİFT.1, TEK/ÇİFT.2, PLUS.1, PLUS.2, MINUS.1, MINUS.2, 5_V_DC.GND, Relay_5V1.connector2, Relay_5V2.connector2
  VCC: GLCD_128x1.2_Vdd, GLCD_128x1.17_RST, GLCD_128x1.19_A(+), Arduino_Mini_Pro_Rev14.VCC, 5_V_DC.VCC, Relay_5V1.connector1, Relay_5V2.connector1
  N3: GLCD_128x1.4_D/I, Arduino_Mini_Pro_Rev14.A3
  N4: GLCD_128x1.5_R/W, Arduino_Mini_Pro_Rev14.A2
  N5: GLCD_128x1.6_Enable, Arduino_Mini_Pro_Rev14.A4
  N6: GLCD_128x1.7_DB0, Arduino_Mini_Pro_Rev14.D8
  N7: GLCD_128x1.8_DB1, Arduino_Mini_Pro_Rev14.D9
  N8: GLCD_128x1.9_BD2, Arduino_Mini_Pro_Rev14.D10
  N9: GLCD_128x1.10_DB3, Arduino_Mini_Pro_Rev14.MOSI
  N10: GLCD_128x1.11_DB4, Arduino_Mini_Pro_Rev14.D4
  N11: GLCD_128x1.12_DB5, Arduino_Mini_Pro_Rev14.D5
  N12: GLCD_128x1.13_DB6, Arduino_Mini_Pro_Rev14.D6
  N13: GLCD_128x1.14_DB7, Arduino_Mini_Pro_Rev14.D7
  N14: GLCD_128x1.15_CS1, Arduino_Mini_Pro_Rev14.A0
  N15: GLCD_128x1.16_CS2, Arduino_Mini_Pro_Rev14.A1
  N16: Arduino_Mini_Pro_Rev14.SCK, Relay_5V2.connector0
  N17: Arduino_Mini_Pro_Rev14.D2, Relay_5V1.connector0
  N18: Relay_5V1.connector5, Relay_5V2.connector5, 12_V_DC.VCC

notes:
  +5 RED
  GND BLACK
  SAME COLOR CONECTED
  1 VSS - GND
  2 VDD - 5V +
  3 V0 - (contrast)
  4 RS - A3
  5 R/W - A2
  6 E - A4
  7 DB0 - 8
  8 DB1 - 9
  9 DB2 - 10
  10 DB3 - 11
  11 DB4 - 4
  12 DB5 - 5
  13 DB6 - 6
  14 DB7 - 7
  15 CS1 - A0
  16 CS2 - A1
  17 RST - 5V +
  18 VOUT - ( contrast)
  19 BLA - 5V +
  20 BLK - GND
